# Fritzing sketch esp8266_sensors (saved by Fritzing 0.9.3b)
circuit board: 4.99706cm x 4.98238cm
perfboards: 1

parts:
  IC1 = Voltage Regulator [package=to-92]
  S1 = Pushbutton [package="[THT]"]
  J3 = male pin header, 2 pins [form="♂ (male)"]
  J5 = female pin header, 6 pins [form="♀ (female)"]
  R2 = Resistor [tolerance=±5% resistance=10k package=THT]
  R3 = Resistor [tolerance=±5% resistance=10k package=THT]
  J7 = Screw terminal - 2 pins [package=THT]
  R4 = Resistor [tolerance=±5% resistance=330k package=THT]
  J2 = male pin header, 2 pins [form="♂ (male)"]
  C1 = Tantalum Capacitor [capacitance=2.2µF package="100 mil [THT, tantalum]"]
  C2 = Tantalum Capacitor [capacitance=2.2µF package="100 mil [THT, tantalum]"]
  U5 = mystery part, 6 pins [chip_label=?]
  U6 = mystery part, 6 pins [chip_label=?]
  U7 = mystery part, 6 pins [chip_label=?]
  DHT1 = DHT22_Humidity_and_Temperature_Sensor
  Q1 = Basic FET N-Channel [package="TO220 [THT]"]
  R6 = Resistor [tolerance=±5% resistance=100k package=THT]
  J4 = female pin header, 2 pins [form="♀ (female)"]
  U11 = mystery part, 6 pins [chip_label=?]
  U12 = mystery part, 6 pins [chip_label=?]
  R1 = Resistor [tolerance=±5% resistance=10k package=THT]
  R5 = Resistor [tolerance=±5% resistance=47k package=THT]
  U10 = mystery part, 9 pins [chip_label=?]
  U9 = mystery part, 9 pins [chip_label=?]
  U8 = mystery part, 9 pins [chip_label=?]
  J6 = female pin header, 11 pins [form="♀ (female)"]
  J1 = male pin header, 2 pins [form="♂ (male)"]
  ESP1 = mystery part, 22 pins [chip_label=ESP-mod]

nets:
  GND: IC1.GND, S1.Pin_1, S1.Pin_2, J5.pin1, J7.pin1, C1.-, C2.-, DHT1.connector4, Q1.source, R6.Pin_0, R5.Pin_0, J6.pin10, ESP1.pin2
  N1: IC1.IN, J7.pin2, C2.+, J1.pin1
  3V3: IC1.OUT, R2.Pin_0, R3.Pin_0, C1.+, DHT1.connector1, R1.Pin_0, J6.pin11, ESP1.pin1
  RSTB: S1.Pin_3, S1.Pin_4, J3.pin1, ESP1.pin13
  GPIO16: J3.pin2, ESP1.pin15
  GPIO3: J5.pin4, ESP1.pin4
  GPIO1: J5.pin5, ESP1.pin3
  GPIO4: R2.Pin_1, J6.pin7, ESP1.pin22
  GPIO5: R3.Pin_1, J6.pin8, ESP1.pin11
  N2: R4.Pin_0, J1.pin2
  N3: R4.Pin_1, J2.pin1, R5.Pin_1
  ADC: J2.pin2, ESP1.pin12
  N4: U5.pin1, U5.pin2, U5.pin3
  N5: U5.pin4, U5.pin5, U5.pin6
  N6: U6.pin1, U6.pin2, U6.pin3
  N7: U6.pin4, U6.pin5, U6.pin6
  N8: U7.pin1, U7.pin2, U7.pin3
  N9: U7.pin4, U7.pin5, U7.pin6
  GPIO13: DHT1.connector2, R1.Pin_1, J6.pin3, ESP1.pin18
  N10: Q1.gate, R6.Pin_1, J4.pin2
  GNDSW: Q1.drain, J6.pin9
  GPIO15: J4.pin1, J6.pin4, ESP1.pin19
  N11: U11.pin1, U11.pin2, U11.pin3
  N12: U11.pin4, U11.pin5, U11.pin6
  N13: U12.pin1, U12.pin2, U12.pin3
  N14: U12.pin4, U12.pin5, U12.pin6
  N15: U10.pin1, U10.pin2, U10.pin3
  N16: U10.pin4, U10.pin5, U10.pin6
  N17: U10.pin7, U10.pin8, U10.pin9
  N18: U9.pin1, U9.pin2, U9.pin3
  N19: U9.pin4, U9.pin5, U9.pin6
  N20: U9.pin7, U9.pin8, U9.pin9
  N21: U8.pin1, U8.pin2, U8.pin3
  N22: U8.pin4, U8.pin5, U8.pin6
  N23: U8.pin7, U8.pin8, U8.pin9
  GPIO12: J6.pin1, ESP1.pin16
  GPIO14: J6.pin2, ESP1.pin17
  GPIO2: J6.pin5, ESP1.pin20
  GPIO0: J6.pin6, ESP1.pin21

notes:
  GND
  CTS
  POWER
  TXO
  RXI
  DTR
  GPIO1: U0TXD -> RXI
  GPIO3: U0RXD -> TXO
  RESET
  IC1: MCP1700-3302E/TO
  C1 and C2: 2.2µF
  Prototype Area
  Bridge J2 to measure bat voltage
  3V3
  GND
  GNDSW
  GPIO5
  GPIO4
  GPIO0
  GPIO2
  GPIO15
  GPIO13
  GPIO14
  GPIO12
  SCL
  TXO
  RXI
  +
  -
  SDA
  ADC
  GPIO16
  CLK
  MOSI
  MISO
  3.5V-6V
  computerlinguist.org
  ESP8266 Sensor Board
